# Fritzing sketch connections (saved by Fritzing 0.8.7b)
breadboards: 1

parts:
  부품1 = FC-28 Soil Hygrometer Module - Probe
  부품2 = FC-28 Soil Hygrometer Module
  Part2 = GUVA-S12SD UV Light Sensor
  Part3 = Adafruit T-Cobbler Plus [part_number="Adafruit #1989 and #2028"]
  IC1 = MCP3008 8-channel 10-bit ADC [part_number=MCP3008]

nets:
  N1: 부품1.POS, 부품2.POS
  N2: 부품1.NEG, 부품2.NEG
  VCC: 부품2.VCC, Part2.5V, Part3.+5V, IC1.no_name_yet#15, IC1.no_name_yet#16
  GND: 부품2.GND, Part2.Out, Part3.GND, IC1.no_name_yet#9, IC1.no_name_yet#14
  N3: 부품2.AO, IC1.no_name_yet#1
  N4: Part2.GND, IC1.no_name_yet#2
  N5: Part3.MOSI, IC1.no_name_yet#11
  N6: Part3.MISO, IC1.no_name_yet#12
  N7: Part3.SCLK, IC1.no_name_yet#13
  N8: Part3.CE0, IC1.no_name_yet#10

custom parts:
  FC-28 Soil Hygrometer Module - Probe: The FC-28 is a soil hygrometer module that uses the Texas Instruments LM393 comparator chip to provide an analog measurement of soil humidity.
  FC-28 Soil Hygrometer Module: The FC-28 is a soil hygrometer module that uses the Texas Instruments LM393 comparator chip to provide an analog measurement of soil humidity. The digital output is high when soil moisture is over a certain threshold, as determined by adjusting the potentiometer.
  GUVA-S12SD UV Light Sensor: Extend your light-sensing spectrum with this analog UV sensor module. It uses a UV photodiode, which can detect the 240-370nm range of light (which covers UVB and most of UVA spectrum). The signal level from the photodiode is very small, in the nano-ampere level, so we tossed on an opamp to amplify the signal to a more manageable volt-level.
  Adafruit T-Cobbler Plus: The Raspberry Pi has landed on the Maker World like a 40-GPIO pinned, quad-USB ported, credit card sized bomb of DIY joy. And while you can use most of our great Model B accessories by hooking up our downgrade cable, its probably a good time to upgrade your set up and accessorize using all of the 40 pins. That's why we now carry the Assembled Adafruit Pi T-Cobbler Plus - Breakout + Cable for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
